# Fritzing sketch project-setup (saved by Fritzing 0.9.3b)
circuit board: 4.74536cm x 6.54332cm
breadboards: 1

parts:
  R1 = Resistor [tolerance=±5% resistance=250 package=THT]
  Raspberry_Pi_1 = Raspberry Pi 3 [part_number=RPI-3-V1.2]
  R2 = Resistor [tolerance=±5% resistance=250 package=THT]
  R3 = Resistor [tolerance=±5% resistance=250 package=THT]
  R4 = Resistor [tolerance=±5% resistance=1k package=THT]
  R5 = Resistor [tolerance=±5% resistance=1k package=THT]
  S1 = Pushbutton [package="[THT]"]
  LED9 = LED - 5mm [color="Red (633nm)" package="5 mm [THT]"]
  LED10 = LED - 5mm [color="Green (565nm)" package="5 mm [THT]"]
  LED11 = LED - 5mm [color="Blue (470nm)" package="5 mm [THT]"]
  BMP085 = Barometric Pressure Sensor - BMP085 Breakout
  S2 = Pushbutton [package="[THT]"]

nets:
  GND: R1.Pin_0, Raspberry_Pi_1.GND, R2.Pin_0, R3.Pin_0, R4.Pin_0, R5.Pin_0, BMP085.GND
  N1: R1.Pin_1, LED9.cathode
  3V3: Raspberry_Pi_1.3v3, Raspberry_Pi_1.3V3, S1.Pin_1, S1.Pin_2, BMP085.VCC, S2.Pin_1, S2.Pin_2
  N2: Raspberry_Pi_1.GPIO2, BMP085.SDA
  N3: Raspberry_Pi_1.GPIO3, BMP085.SCL
  N4: Raspberry_Pi_1.GIPO17, R4.Pin_1, S1.Pin_3, S1.Pin_4
  N5: Raspberry_Pi_1.GIPO27, R5.Pin_1, S2.Pin_3, S2.Pin_4
  N6: Raspberry_Pi_1.GIPO22, LED10.anode
  N7: Raspberry_Pi_1.GIPO18, LED9.anode
  N8: Raspberry_Pi_1.GIPO14, LED11.anode
  N9: R2.Pin_1, LED10.cathode
  N10: R3.Pin_1, LED11.cathode
